// Logisim project RippleCarry.circ as structural Verilog: 2 circuits, main circuit main
module main (
  input  in_1,
  input  in_2,
  input  in_3,
  input  in_4,
  input  in_5,
  input  in_6,
  output out_7,
  output out_8,
  output out_9,
  output out_10
);

  wire fulladder_1_out_5, fulladder_2_out_5;

  FullAdder fulladder_1 (.in_2(in_1), .in_3(in_2), .out_4(out_7), .out_5(fulladder_1_out_5));  // open: in_1
  FullAdder fulladder_2 (.in_1(fulladder_1_out_5), .in_2(in_3), .in_3(in_4), .out_4(out_8), .out_5(fulladder_2_out_5));
  FullAdder fulladder_3 (.in_1(fulladder_2_out_5), .in_2(in_5), .in_3(in_6), .out_4(out_9), .out_5(out_10));
endmodule

module FullAdder (
  input  in_1,
  input  in_2,
  input  in_3,
  output out_4,
  output out_5
);

  wire and_1_out, and_2_out, and_3_out, xor_2_out;

  xor xor_1 (out_4, in_3, xor_2_out);
  xor xor_2 (xor_2_out, in_2, in_1);
  and and_1 (and_1_out, in_2, in_1);
  and and_2 (and_2_out, in_3, in_2);
  and and_3 (and_3_out, in_3, in_1);
  or or_1 (out_5, and_1_out, and_2_out, and_3_out);

  // Notes on the sheet:
  //   A
  //   B
  //   Cin0
endmodule
