// Logisim project jokenpo.circ as structural Verilog: 4 circuits, main circuit main
module main (
  input  in_1,
  input  in_2,
  input  in_3,
  input  in_4,
  input  in_5,
  input  in_6,
  output out_7,
  output out_8,
  output out_9
);

  wire CodificadorJogador1_s1, CodificadorJogador1_s2, CodificadorJogador2_s1, CodificadorJogador2_s2,
       Jogo_s1, Jogo_s2;

  mod1 CodificadorJogador1 (
    .Pedra(in_1), .Papel(in_2), .Tesoura(in_3), .S1(CodificadorJogador1_s1), .S2(CodificadorJogador1_s2));
  mod1 CodificadorJogador2 (
    .Pedra(in_4), .Papel(in_5), .Tesoura(in_6), .S1(CodificadorJogador2_s1), .S2(CodificadorJogador2_s2));
  mod2 Jogo (
    .A(CodificadorJogador1_s1), .B(CodificadorJogador1_s2), .C(CodificadorJogador2_s1),
    .D(CodificadorJogador2_s2), .S1(Jogo_s1), .S2(Jogo_s2));
  mod3 Decodificador (.A(Jogo_s1), .B(Jogo_s2), .Empate(out_7), .Jogador1(out_8), .Jogador2(out_9));
endmodule

module mod1 (
  input  Pedra,
  input  Papel,
  input  Tesoura,
  output S1,
  output S2
);

  wire and_1_out, and_2_out, and_3_out, not_1_out, not_2_out, not_3_out;

  not not_1 (not_1_out, Pedra);
  not not_2 (not_2_out, Papel);
  not not_3 (not_3_out, Tesoura);
  and and_1 (and_1_out, not_1_out, not_2_out, Tesoura);
  and and_2 (and_2_out, not_1_out, Papel, not_3_out);
  and and_3 (and_3_out, Pedra, not_2_out, not_3_out);
  or or_1 (S1, and_1_out, and_2_out);
  or or_2 (S2, and_2_out, and_3_out);

  // Notes on the sheet:
  //   Módulo 1 - Codificador
endmodule

module mod2 (
  input  A,
  input  B,
  input  C,
  input  D,
  output S1,
  output S2
);

  wire and_1_out, and_2_out, and_3_out, and_4_out, and_5_out, and_6_out, and_7_out, and_8_out, not_1_out,
       not_2_out, not_3_out, not_4_out;

  not not_1 (not_1_out, A);
  not not_2 (not_2_out, B);
  not not_3 (not_3_out, C);
  not not_4 (not_4_out, D);
  and and_1 (and_1_out, B, not_3_out, D);
  and and_2 (and_2_out, A, C, D);
  and and_3 (and_3_out, A, not_2_out, C);
  and and_4 (and_4_out, not_1_out, B, C, not_4_out);
  and and_5 (and_5_out, not_1_out, B, D);
  and and_6 (and_6_out, A, B, C);
  and and_7 (and_7_out, A, C, not_4_out);
  and and_8 (and_8_out, A, not_2_out, not_3_out, D);
  or or_1 (S1, and_1_out, and_2_out, and_3_out, and_4_out);
  or or_2 (S2, and_5_out, and_6_out, and_7_out, and_8_out);

  // Notes on the sheet:
  //   Módulo 2 - Jogo
endmodule

module mod3 (
  input  A,
  input  B,
  output Empate,
  output Jogador1,
  output Jogador2
);

  wire not_1_out, not_2_out;

  not not_1 (not_1_out, A);
  not not_2 (not_2_out, B);
  and and_1 (Empate, A, B);
  and and_2 (Jogador1, A, not_2_out);
  and and_3 (Jogador2, not_1_out, B);

  // Notes on the sheet:
  //   Módulo 3 - Decodificador
endmodule
