// Logisim project trabalho_final_circuitos.circ as structural Verilog: 6 circuits, main circuit main
module main (
  input  [7:0] in_1,
  input  [1:0] in_2,
  input  [1:0] in_3,
  input  [1:0] in_4,
  input  Sel_Valor,
  input  in_6,
  input  [2:0] in_7,
  output [7:0] out_8
);

  wire ula_1_c, ula_1_z;
  wire [7:0] bancoregistradores_1_va, bancoregistradores_1_vb, multiplexer_1_out;

  Multiplexer #(.width(8)) multiplexer_1 (.in0(in_1), .in1(out_8), .out(multiplexer_1_out), .sel(Sel_Valor));
  bancoRegistradores bancoregistradores_1 (
    .VA(bancoregistradores_1_va), .VB(bancoregistradores_1_vb), .VW(multiplexer_1_out), .RW(in_4),
    .Escreve(in_6), .RA(in_2), .RB(in_3));
  LED led_1 (.in(ula_1_c));
  LED led_2 (.in(ula_1_z));
  ULA ula_1 (
    .C(ula_1_c), .Z(ula_1_z), .out_6(out_8), .A(bancoregistradores_1_va), .Sel_Op(in_7),
    .B(bancoregistradores_1_vb));
  LED led_3 (.in(out_8[7]));
  LED led_4 (.in(out_8[6]));
  LED led_5 (.in(out_8[5]));
  LED led_6 (.in(out_8[4]));
  LED led_7 (.in(out_8[3]));
  LED led_8 (.in(out_8[2]));
  LED led_9 (.in(out_8[1]));
  LED led_10 (.in(out_8[0]));

  // Notes on the sheet:
  //   Insere Valor
endmodule

module somador1bit (
  input  A,
  input  B,
  input  Cin,
  output S,
  output Cout
);

  wire and_1_out, and_2_out, and_3_out, xor_1_out;

  xor xor_1 (xor_1_out, A, B);
  and and_1 (and_1_out, A, Cin);
  and and_2 (and_2_out, A, B);
  and and_3 (and_3_out, B, Cin);
  xor xor_2 (S, xor_1_out, Cin);
  or or_1 (Cout, and_1_out, and_2_out, and_3_out);
endmodule

module somador8bits (
  input  [7:0] B,
  input  controle,
  input  [7:0] A,
  output Overflow,
  output [7:0] S
);

  wire somador1bit_1_cout, somador1bit_2_cout, somador1bit_3_cout, somador1bit_4_cout, somador1bit_5_cout,
       somador1bit_6_cout, somador1bit_7_cout, somador1bit_8_cout, xor_2_out, xor_3_out, xor_4_out,
       xor_5_out, xor_6_out, xor_7_out, xor_8_out, xor_9_out;

  xor xor_1 (Overflow, somador1bit_2_cout, somador1bit_1_cout);
  somador1bit somador1bit_1 (.A(A[7]), .B(xor_2_out), .Cin(somador1bit_2_cout), .S(S[7]), .Cout(somador1bit_1_cout));
  somador1bit somador1bit_2 (.A(A[6]), .B(xor_3_out), .Cin(somador1bit_3_cout), .S(S[6]), .Cout(somador1bit_2_cout));
  xor xor_2 (xor_2_out, controle, B[7]);
  xor xor_3 (xor_3_out, controle, B[6]);
  xor xor_4 (xor_4_out, controle, B[5]);
  somador1bit somador1bit_3 (.A(A[5]), .B(xor_4_out), .Cin(somador1bit_4_cout), .S(S[5]), .Cout(somador1bit_3_cout));
  xor xor_5 (xor_5_out, controle, B[4]);
  somador1bit somador1bit_4 (.A(A[4]), .B(xor_5_out), .Cin(somador1bit_5_cout), .S(S[4]), .Cout(somador1bit_4_cout));
  xor xor_6 (xor_6_out, controle, B[3]);
  xor xor_7 (xor_7_out, controle, B[2]);
  somador1bit somador1bit_5 (.A(A[3]), .B(xor_6_out), .Cin(somador1bit_6_cout), .S(S[3]), .Cout(somador1bit_5_cout));
  xor xor_8 (xor_8_out, controle, B[1]);
  somador1bit somador1bit_6 (.A(A[2]), .B(xor_7_out), .Cin(somador1bit_7_cout), .S(S[2]), .Cout(somador1bit_6_cout));
  xor xor_9 (xor_9_out, controle, B[0]);
  somador1bit somador1bit_7 (.A(A[1]), .B(xor_8_out), .Cin(somador1bit_8_cout), .S(S[1]), .Cout(somador1bit_7_cout));
  somador1bit somador1bit_8 (.A(A[0]), .B(xor_9_out), .Cin(controle), .S(S[0]), .Cout(somador1bit_8_cout));
endmodule

module bancoRegistradores (
  input  [1:0] RA,
  input  [7:0] VW,
  input  [1:0] RB,
  input  [1:0] RW,
  input  Escreve,
  output [7:0] VA,
  output [7:0] VB
);

  wire demultiplexer_2_out0, demultiplexer_2_out1, demultiplexer_2_out2, demultiplexer_2_out3;
  wire [7:0] demultiplexer_1_out0, demultiplexer_1_out1, demultiplexer_1_out2, demultiplexer_1_out3,
       register_1_q, register_2_q, register_3_q, register_4_q;

  Demultiplexer #(.select(2), .width(8)) demultiplexer_1 (
    .out0(demultiplexer_1_out0), .out1(demultiplexer_1_out1), .out2(demultiplexer_1_out2),
    .out3(demultiplexer_1_out3), .in(VW), .sel(RW));
  Demultiplexer #(.select(2)) demultiplexer_2 (
    .out0(demultiplexer_2_out0), .out1(demultiplexer_2_out1), .out2(demultiplexer_2_out2),
    .out3(demultiplexer_2_out3), .in(Escreve), .sel(RW));
  Register register_1 (.D(demultiplexer_1_out0), .clk(demultiplexer_2_out0), .Q(register_1_q), .clr(1'b0));  // open: en
  Register register_2 (.D(demultiplexer_1_out1), .clk(demultiplexer_2_out1), .Q(register_2_q), .clr(1'b0));  // open: en
  Register register_3 (.D(demultiplexer_1_out2), .clk(demultiplexer_2_out2), .Q(register_3_q), .clr(1'b0));  // open: en
  Register register_4 (.D(demultiplexer_1_out3), .clk(demultiplexer_2_out3), .Q(register_4_q), .clr(1'b0));  // open: en
  Multiplexer #(.select(2), .width(8)) multiplexer_1 (
    .in0(register_1_q), .in1(register_2_q), .in2(register_3_q), .in3(register_4_q), .out(VA), .sel(RA));
  Multiplexer #(.select(2), .width(8)) multiplexer_2 (
    .in0(register_1_q), .in1(register_2_q), .in2(register_3_q), .in3(register_4_q), .out(VB), .sel(RB));
endmodule

module ULA (
  input  [7:0] B,
  input  [7:0] A,
  input  [2:0] Sel_Op,
  output C,
  output Z,
  output [7:0] out_6
);

  wire orentrebits_1_s, orentrebits_2_s, orentrebits_3_s, somador8bits_1_overflow, somador8bits_2_overflow;
  wire [7:0] and_1_out, divider_1_out, divider_1_rem, multiplexer_2_out, multiplier_1_cout, multiplier_1_out,
       not_1_out, or_1_out, somador8bits_1_s, somador8bits_2_s, xor_1_out;

  Multiplier multiplier_1 (.a(B), .b(A), .out(multiplier_1_out), .cout(multiplier_1_cout));  // open: cin
  assign not_1_out = ~A;  // NOT_Gate not_1, 8 bits wide
  orEntreBits orentrebits_1 (.S(orentrebits_1_s), .in_1(multiplier_1_cout));
  assign xor_1_out = A ^ B;  // XOR_Gate xor_1, 8 bits wide
  somador8bits somador8bits_1 (.B(B), .controle(1'b0), .A(A), .Overflow(somador8bits_1_overflow), .S(somador8bits_1_s));
  Multiplexer #(.select(3), .width(8)) multiplexer_1 (
    .in0(multiplier_1_out), .in1(not_1_out), .in2(xor_1_out), .in3(somador8bits_1_s), .in4(or_1_out),
    .in5(divider_1_out), .in6(somador8bits_2_s), .in7(and_1_out), .out(out_6), .sel(Sel_Op));
  assign or_1_out = A | B;  // OR_Gate or_1, 8 bits wide
  Divider divider_1 (.a(A), .b(B), .out(divider_1_out), .rem(divider_1_rem));  // open: upper
  orEntreBits orentrebits_2 (.S(orentrebits_2_s), .in_1(divider_1_rem));
  somador8bits somador8bits_2 (.B(B), .controle(1'b1), .A(A), .Overflow(somador8bits_2_overflow), .S(somador8bits_2_s));
  assign and_1_out = A & B;  // AND_Gate and_1, 8 bits wide
  Multiplexer #(.select(3), .width(8)) multiplexer_2 (
    .in0(multiplier_1_out), .in1(not_1_out), .in2(xor_1_out), .in3(somador8bits_1_s), .in4(or_1_out),
    .in5(divider_1_out), .in6(somador8bits_2_s), .in7(and_1_out), .out(multiplexer_2_out), .sel(Sel_Op));
  orEntreBits orentrebits_3 (.S(orentrebits_3_s), .in_1(multiplexer_2_out));
  Multiplexer #(.select(3)) multiplexer_3 (
    .in0(orentrebits_1_s), .in1(1'b0), .in2(1'b0), .in3(somador8bits_1_overflow), .in4(1'b0),
    .in5(orentrebits_2_s), .in6(somador8bits_2_overflow), .in7(1'b0), .out(C), .sel(Sel_Op));
  not not_2 (Z, orentrebits_3_s);

  // Notes on the sheet:
  //   A * B
  //   NOT A
  //   A XOR B
  //   A + B
  //   A OR B
  //   A / B
  //   A - B
  //   A AND B
endmodule

module orEntreBits (
  input  [7:0] in_1,
  output S
);

  or or_1 (S, in_1[0], in_1[1], in_1[2], in_1[3], in_1[4], in_1[5], in_1[6], in_1[7]);
endmodule
